// Digital circuit Template-04.dig as structural Verilog
module Template_04 (
  input  [6:0] In,
  output [6:0] Output
);

  wire C1, C2, C3, S1, S2, S3, S4, S5, S6, S7;

  xor xor_1 (C1, In[3], In[2], In[1], In[0]);
  xor xor_2 (C2, In[5], In[4], In[1], In[0]);
  xor xor_3 (C3, In[6], In[4], In[2], In[0]);
  Demultiplexer #(.Selector_Bits(3)) demultiplexer_1 (
    .sel({C1, C2, C3}), .in(1'b1), .out_1(S1), .out_2(S2), .out_3(S3), .out_4(S4), .out_5(S5), .out_6(S6),
    .out_7(S7));  // open: out_0
  assign Output = In ^ {S1, S2, S3, S4, S5, S6, S7};  // XOr xor_4, 7 bits wide

  // Other names for the same wires on the sheet: H[2:0] = {C1, C2, C3}; _7 = In[0]; _6 = In[1]; _5 = In[2];
  //   _4 = In[3]; _3 = In[4]; _2 = In[5]; _1 = In[6]
endmodule
